// Digital circuit SOP.dig as structural Verilog
module SOP (
  input  A,
  input  B,
  input  C,
  input  D,
  output Y
);

  wire and_1_out, not_1_out, or_1_out;

  or or_1 (or_1_out, D, A);
  and and_1 (and_1_out, D, A);
  not not_1 (not_1_out, and_1_out);
  and and_2 (Y, not_1_out, or_1_out);

  // Notes on the sheet:
  //   A: MSB
  //   D: LSB
  //   Use A as the most-significant bit and 
  //   D as the least-significant bit.
endmodule

/* Test case:
A B C D Y
0 0 0 0 X
0 0 0 1 1
*/
